// Logisim project 8bitsProcesador.circ as structural Verilog
module ALU (
  input  [7:0] A,
  input  [7:0] B,
  input  [1:0] ALU_Opt,
  output Zero,
  output [7:0] ALU_Respuesta
);

  wire [7:0] adder_1_out, and_1_out, or_1_out, subtractor_1_out;

  Adder adder_1 (.a(A), .b(B), .out(adder_1_out));  // open: cin, cout
  Subtractor subtractor_1 (.a(A), .b(B), .out(subtractor_1_out));  // open: bin, bout
  assign and_1_out = A & B;  // AND_Gate and_1, 8 bits wide
  assign or_1_out = A | B;  // OR_Gate or_1, 8 bits wide
  Multiplexer #(.select(2), .width(8)) multiplexer_1 (
    .in0(adder_1_out), .in1(subtractor_1_out), .in2(and_1_out), .in3(or_1_out), .out(ALU_Respuesta),
    .sel(ALU_Opt));  // open: en
  Comparator comparator_1 (.a({8{1'b0}}), .b(ALU_Respuesta), .eq(Zero));  // open: gt, lt
endmodule

module ALUControl (
  input  [1:0] ALUOp,
  input  [2:0] \Finción ,
  output [1:0] \Operación 
);

  wire and_1_out, not_1_out;

  not not_1 (not_1_out, ALUOp[0]);
  and and_1 (and_1_out, not_1_out, ALUOp[1]);
  Multiplexer multiplexer_1 (.in0(ALUOp[0]), .in1(\Finción [0]), .out(\Operación [0]), .sel(and_1_out));  // open: en
  Multiplexer multiplexer_2 (.in0(ALUOp[1]), .in1(\Finción [1]), .out(\Operación [1]), .sel(and_1_out));  // open: en
endmodule
